// Logisim project 32bit_CPU_Program1.circ as structural Verilog: 6 circuits, main circuit main
module main (
);

  wire ALU_zero_flag, clock_1_out, Control_alusrc, Control_branch, Control_jump, Control_memread,
       Control_memtoreg, Control_memwrite, Control_regdst, Control_regwrite;
  wire [1:0] Control_aluop;
  wire [3:0] ALU_Control_alu_control_out;
  wire [4:0] multiplexer_1_out;
  wire [23:0] ALU_result;
  wire [27:0] rom_1_data;
  wire [31:0] bit_extender_1_out, multiplexer_2_out, multiplexer_3_out, PC_pc_out, ram_1_data,
       Reg_File_reg_data_1, Reg_File_reg_data_2;
  wire [31:24] ALU_result_2;
  wire [31:28] rom_1_data_2;

  PC PC (
    .Sign_Extend(bit_extender_1_out), ._28bit_from_Istr_Mem(rom_1_data), .PC_Out(PC_pc_out),
    .Branch_Control(Control_branch), .Zero_from_ALU(ALU_zero_flag), .Jump_Control(Control_jump));
  ROM #(.dataWidth(32)) rom_1 (.addr(PC_pc_out[7:0]), .data({rom_1_data_2, rom_1_data}));  // open: sel
  assign bit_extender_1_out = {{16{rom_1_data[15]}}, rom_1_data[15:0]};  // Bit_Extender bit_extender_1
  Control Control (
    .Control_In({rom_1_data_2, rom_1_data[27:26]}), .Jump(Control_jump), .RegDst(Control_regdst),
    .Branch(Control_branch), .MemRead(Control_memread), .MemToReg(Control_memtoreg),
    .MemWrite(Control_memwrite), .ALUSrc(Control_alusrc), .ALUOp(Control_aluop), .RegWrite(Control_regwrite));
  Multiplexer #(.width(5), .enable("false")) multiplexer_1 (
    .in0(rom_1_data[20:16]), .in1(rom_1_data[15:11]), .out(multiplexer_1_out), .sel(Control_regdst));
  ALUControl ALU_Control (
    ._6bitfromISTR(rom_1_data[5:0]), .ALUOp(Control_aluop), .ALU_Control_Out(ALU_Control_alu_control_out));
  Reg_File Reg_File (
    .Write_Reg(multiplexer_1_out), .Reg_Write(Control_regwrite), .Write_Data(multiplexer_3_out),
    .Read_Reg_1(rom_1_data[25:21]), .Read_Reg_2(rom_1_data[20:16]), .Reg_Data_1(Reg_File_reg_data_1),
    .Reg_Data_2(Reg_File_reg_data_2));
  Multiplexer #(.width(32), .enable("false")) multiplexer_2 (
    .in0(Reg_File_reg_data_2), .in1(bit_extender_1_out), .out(multiplexer_2_out), .sel(Control_alusrc));
  ALU ALU (
    .B(multiplexer_2_out), .A(Reg_File_reg_data_1), .Result({ALU_result_2, ALU_result}),
    .ALU_Op(ALU_Control_alu_control_out), .Zero_Flag(ALU_zero_flag));
  Clock clock_1 (.out(clock_1_out));
  RAM #(.addrWidth(24), .dataWidth(32), .bus("separate")) ram_1 (
    .addr(ALU_result), .din(Reg_File_reg_data_2), .data(ram_1_data), .str(Control_memwrite),
    .clk(clock_1_out), .ld(Control_memread));  // open: sel, clr
  Multiplexer #(.width(32), .enable("false")) multiplexer_3 (
    .in0({ALU_result_2, ALU_result}), .in1(ram_1_data), .out(multiplexer_3_out), .sel(Control_memtoreg));

  // Notes on the sheet:
  //   contents of rom_1 (hex, n*v repeats v):
  //   8c010000 8c020001 411820 222022 642824 453025 ac060002 ac030003
endmodule

module PC (
  input  [27:0] _28bit_from_Istr_Mem,
  input  Jump_Control,
  input  [31:0] Sign_Extend,
  input  Zero_from_ALU,
  input  Branch_Control,
  output [31:0] PC_Out
);

  wire and_1_out, Clock_out;
  wire [31:0] adder_1_out, adder_2_out, multiplexer_1_out, multiplexer_2_out;

  Clock Clock (.out(Clock_out));
  Register #(.width(32)) Program_Counter (.D(multiplexer_2_out), .Q(PC_Out), .clk(Clock_out));  // open: en, clr
  Adder #(.width(32)) adder_1 (.a(32'h1), .b(PC_Out), .out(adder_1_out));  // open: cin, cout
  Adder #(.width(32)) adder_2 (.a(adder_1_out), .b(Sign_Extend), .out(adder_2_out));  // open: cin, cout
  Multiplexer #(.width(32), .enable("false")) multiplexer_1 (
    .in0(adder_1_out), .in1(adder_2_out), .out(multiplexer_1_out), .sel(and_1_out));
  and and_1 (and_1_out, Branch_Control, Zero_from_ALU);
  Multiplexer #(.width(32), .disabled(0), .enable("false")) multiplexer_2 (
    .in0(multiplexer_1_out), .in1({adder_1_out[31:28], 2'b00, _28bit_from_Istr_Mem[25:0]}),
    .out(multiplexer_2_out), .sel(Jump_Control));
endmodule

module Reg_File (
  input  [4:0] Read_Reg_1,
  input  [4:0] Write_Reg,
  input  [4:0] Read_Reg_2,
  input  Reg_Write,
  input  [31:0] Write_Data,
  output [31:0] Reg_Data_1,
  output [31:0] Reg_Data_2
);

  wire and_1_out, and_2_out, and_3_out, and_4_out, and_5_out, and_6_out, and_7_out, and_8_out, and_9_out,
       and_10_out, and_11_out, and_12_out, and_13_out, and_14_out, and_15_out, and_16_out, and_17_out,
       and_18_out, and_19_out, and_20_out, and_21_out, and_22_out, and_23_out, and_24_out, and_25_out,
       and_26_out, and_27_out, and_28_out, and_29_out, and_30_out, and_31_out, and_32_out, clock_1_out,
       decoder_1_out0, decoder_1_out1, decoder_1_out2, decoder_1_out3, decoder_1_out4, decoder_1_out5,
       decoder_1_out6, decoder_1_out7, decoder_1_out8, decoder_1_out9, decoder_1_out10, decoder_1_out11,
       decoder_1_out12, decoder_1_out13, decoder_1_out14, decoder_1_out15, decoder_1_out16, decoder_1_out17,
       decoder_1_out18, decoder_1_out19, decoder_1_out20, decoder_1_out21, decoder_1_out22, decoder_1_out23,
       decoder_1_out24, decoder_1_out25, decoder_1_out26, decoder_1_out27, decoder_1_out28, decoder_1_out29,
       decoder_1_out30, decoder_1_out31;
  wire [31:0] register_1_q, register_2_q, register_3_q, register_4_q, register_5_q, register_6_q,
       register_7_q, register_8_q, register_9_q, register_10_q, register_11_q, register_12_q, register_13_q,
       register_14_q, register_15_q, register_16_q, register_17_q, register_18_q, register_19_q,
       register_20_q, register_21_q, register_22_q, register_23_q, register_24_q, register_25_q,
       register_26_q, register_27_q, register_28_q, register_29_q, register_30_q, register_31_q,
       register_32_q;

  Decoder #(.select(5)) decoder_1 (
    .out0(decoder_1_out0), .out1(decoder_1_out1), .out2(decoder_1_out2), .out3(decoder_1_out3),
    .out4(decoder_1_out4), .out5(decoder_1_out5), .out6(decoder_1_out6), .out7(decoder_1_out7),
    .out8(decoder_1_out8), .out9(decoder_1_out9), .out10(decoder_1_out10), .out11(decoder_1_out11),
    .out12(decoder_1_out12), .out13(decoder_1_out13), .out14(decoder_1_out14), .out15(decoder_1_out15),
    .out16(decoder_1_out16), .out17(decoder_1_out17), .out18(decoder_1_out18), .out19(decoder_1_out19),
    .out20(decoder_1_out20), .out21(decoder_1_out21), .out22(decoder_1_out22), .out23(decoder_1_out23),
    .out24(decoder_1_out24), .out25(decoder_1_out25), .out26(decoder_1_out26), .out27(decoder_1_out27),
    .out28(decoder_1_out28), .out29(decoder_1_out29), .out30(decoder_1_out30), .out31(decoder_1_out31),
    .sel(Write_Reg));  // open: en
  and and_1 (and_1_out, decoder_1_out0, Reg_Write);
  and and_2 (and_2_out, decoder_1_out1, Reg_Write);
  and and_3 (and_3_out, decoder_1_out2, Reg_Write);
  and and_4 (and_4_out, decoder_1_out3, Reg_Write);
  and and_5 (and_5_out, decoder_1_out4, Reg_Write);
  and and_6 (and_6_out, decoder_1_out5, Reg_Write);
  and and_7 (and_7_out, decoder_1_out6, Reg_Write);
  and and_8 (and_8_out, decoder_1_out7, Reg_Write);
  and and_9 (and_9_out, decoder_1_out8, Reg_Write);
  and and_10 (and_10_out, decoder_1_out9, Reg_Write);
  and and_11 (and_11_out, decoder_1_out10, Reg_Write);
  and and_12 (and_12_out, decoder_1_out11, Reg_Write);
  and and_13 (and_13_out, decoder_1_out12, Reg_Write);
  and and_14 (and_14_out, decoder_1_out13, Reg_Write);
  and and_15 (and_15_out, decoder_1_out14, Reg_Write);
  and and_16 (and_16_out, decoder_1_out15, Reg_Write);
  Register #(.width(32)) register_1 (.D(Write_Data), .en(and_1_out), .Q(register_1_q), .clk(clock_1_out));  // open: clr
  Register #(.width(32)) register_2 (.D(Write_Data), .en(and_2_out), .Q(register_2_q), .clk(clock_1_out));  // open: clr
  Register #(.width(32)) register_3 (.D(Write_Data), .en(and_3_out), .Q(register_3_q), .clk(clock_1_out));  // open: clr
  Register #(.width(32)) register_4 (.D(Write_Data), .en(and_4_out), .Q(register_4_q), .clk(clock_1_out));  // open: clr
  Register #(.width(32)) register_5 (.D(Write_Data), .en(and_5_out), .Q(register_5_q), .clk(clock_1_out));  // open: clr
  Register #(.width(32)) register_6 (.D(Write_Data), .en(and_6_out), .Q(register_6_q), .clk(clock_1_out));  // open: clr
  Register #(.width(32)) register_7 (.D(Write_Data), .en(and_7_out), .Q(register_7_q), .clk(clock_1_out));  // open: clr
  Register #(.width(32)) register_8 (.D(Write_Data), .en(and_8_out), .Q(register_8_q), .clk(clock_1_out));  // open: clr
  Register #(.width(32)) register_9 (.D(Write_Data), .en(and_9_out), .Q(register_9_q), .clk(clock_1_out));  // open: clr
  Register #(.width(32)) register_10 (
    .D(Write_Data), .en(and_10_out), .Q(register_10_q), .clk(clock_1_out));  // open: clr
  Register #(.width(32)) register_11 (
    .D(Write_Data), .en(and_11_out), .Q(register_11_q), .clk(clock_1_out));  // open: clr
  Register #(.width(32)) register_12 (
    .D(Write_Data), .en(and_12_out), .Q(register_12_q), .clk(clock_1_out));  // open: clr
  Register #(.width(32)) register_13 (
    .D(Write_Data), .en(and_13_out), .Q(register_13_q), .clk(clock_1_out));  // open: clr
  Register #(.width(32)) register_14 (
    .D(Write_Data), .en(and_14_out), .Q(register_14_q), .clk(clock_1_out));  // open: clr
  Register #(.width(32)) register_15 (
    .D(Write_Data), .en(and_15_out), .Q(register_15_q), .clk(clock_1_out));  // open: clr
  Register #(.width(32)) register_16 (
    .D(Write_Data), .en(and_16_out), .Q(register_16_q), .clk(clock_1_out));  // open: clr
  Clock clock_1 (.out(clock_1_out));
  and and_17 (and_17_out, decoder_1_out16, Reg_Write);
  and and_18 (and_18_out, decoder_1_out17, Reg_Write);
  and and_19 (and_19_out, decoder_1_out18, Reg_Write);
  and and_20 (and_20_out, decoder_1_out19, Reg_Write);
  and and_21 (and_21_out, decoder_1_out20, Reg_Write);
  and and_22 (and_22_out, decoder_1_out21, Reg_Write);
  and and_23 (and_23_out, decoder_1_out22, Reg_Write);
  and and_24 (and_24_out, decoder_1_out23, Reg_Write);
  and and_25 (and_25_out, decoder_1_out24, Reg_Write);
  and and_26 (and_26_out, decoder_1_out25, Reg_Write);
  and and_27 (and_27_out, decoder_1_out26, Reg_Write);
  and and_28 (and_28_out, decoder_1_out27, Reg_Write);
  and and_29 (and_29_out, decoder_1_out28, Reg_Write);
  and and_30 (and_30_out, decoder_1_out29, Reg_Write);
  and and_31 (and_31_out, decoder_1_out30, Reg_Write);
  and and_32 (and_32_out, decoder_1_out31, Reg_Write);
  Register #(.width(32)) register_17 (
    .D(Write_Data), .en(and_17_out), .Q(register_17_q), .clk(clock_1_out));  // open: clr
  Register #(.width(32)) register_18 (
    .D(Write_Data), .en(and_18_out), .Q(register_18_q), .clk(clock_1_out));  // open: clr
  Register #(.width(32)) register_19 (
    .D(Write_Data), .en(and_19_out), .Q(register_19_q), .clk(clock_1_out));  // open: clr
  Register #(.width(32)) register_20 (
    .D(Write_Data), .en(and_20_out), .Q(register_20_q), .clk(clock_1_out));  // open: clr
  Register #(.width(32)) register_21 (
    .D(Write_Data), .en(and_21_out), .Q(register_21_q), .clk(clock_1_out));  // open: clr
  Register #(.width(32)) register_22 (
    .D(Write_Data), .en(and_22_out), .Q(register_22_q), .clk(clock_1_out));  // open: clr
  Register #(.width(32)) register_23 (
    .D(Write_Data), .en(and_23_out), .Q(register_23_q), .clk(clock_1_out));  // open: clr
  Register #(.width(32)) register_24 (
    .D(Write_Data), .en(and_24_out), .Q(register_24_q), .clk(clock_1_out));  // open: clr
  Register #(.width(32)) register_25 (
    .D(Write_Data), .en(and_25_out), .Q(register_25_q), .clk(clock_1_out));  // open: clr
  Register #(.width(32)) register_26 (
    .D(Write_Data), .en(and_26_out), .Q(register_26_q), .clk(clock_1_out));  // open: clr
  Register #(.width(32)) register_27 (
    .D(Write_Data), .en(and_27_out), .Q(register_27_q), .clk(clock_1_out));  // open: clr
  Register #(.width(32)) register_28 (
    .D(Write_Data), .en(and_28_out), .Q(register_28_q), .clk(clock_1_out));  // open: clr
  Register #(.width(32)) register_29 (
    .D(Write_Data), .en(and_29_out), .Q(register_29_q), .clk(clock_1_out));  // open: clr
  Register #(.width(32)) register_30 (
    .D(Write_Data), .en(and_30_out), .Q(register_30_q), .clk(clock_1_out));  // open: clr
  Register #(.width(32)) register_31 (
    .D(Write_Data), .en(and_31_out), .Q(register_31_q), .clk(clock_1_out));  // open: clr
  Register #(.width(32)) register_32 (
    .D(Write_Data), .en(and_32_out), .Q(register_32_q), .clk(clock_1_out));  // open: clr
  Multiplexer #(.select(5), .width(32)) multiplexer_1 (
    .in0(register_1_q), .in1(register_2_q), .in2(register_3_q), .in3(register_4_q), .in4(register_5_q),
    .in5(register_6_q), .in6(register_7_q), .in7(register_8_q), .in8(register_9_q), .in9(register_10_q),
    .in10(register_11_q), .in11(register_12_q), .in12(register_13_q), .in13(register_14_q),
    .in14(register_15_q), .in15(register_16_q), .in16(register_17_q), .in17(register_18_q),
    .in18(register_19_q), .in19(register_20_q), .in20(register_21_q), .in21(register_22_q),
    .in22(register_23_q), .in23(register_24_q), .in24(register_25_q), .in25(register_26_q),
    .in26(register_27_q), .in27(register_28_q), .in28(register_29_q), .in29(register_30_q),
    .in30(register_31_q), .in31(register_32_q), .out(Reg_Data_1), .sel(Read_Reg_1));  // open: en
  Multiplexer #(.select(5), .width(32)) multiplexer_2 (
    .in0(register_1_q), .in1(register_2_q), .in2(register_3_q), .in3(register_4_q), .in4(register_5_q),
    .in5(register_6_q), .in6(register_7_q), .in7(register_8_q), .in8(register_9_q), .in9(register_10_q),
    .in10(register_11_q), .in11(register_12_q), .in12(register_13_q), .in13(register_14_q),
    .in14(register_15_q), .in15(register_16_q), .in16(register_17_q), .in17(register_18_q),
    .in18(register_19_q), .in19(register_20_q), .in20(register_21_q), .in21(register_22_q),
    .in22(register_23_q), .in23(register_24_q), .in24(register_25_q), .in25(register_26_q),
    .in26(register_27_q), .in27(register_28_q), .in28(register_29_q), .in29(register_30_q),
    .in30(register_31_q), .in31(register_32_q), .out(Reg_Data_2), .sel(Read_Reg_2));  // open: en
endmodule

module ALU (
  input  [31:0] B,
  input  [31:0] A,
  input  [3:0] ALU_Op,
  output [31:0] Result,
  output Zero_Flag
);

  wire [31:0] adder_1_out, and_1_out, or_1_out, subtractor_1_out;

  assign and_1_out = A & B;  // AND_Gate and_1, 32 bits wide
  assign or_1_out = A | B;  // OR_Gate or_1, 32 bits wide
  Adder #(.width(32)) adder_1 (.a(A), .b(B), .out(adder_1_out));  // open: cin, cout
  Subtractor #(.width(32)) subtractor_1 (.a(A), .b(B), .out(subtractor_1_out));  // open: bin, bout
  Multiplexer #(.select(4), .width(32), .enable("false")) multiplexer_1 (
    .in0(and_1_out), .in1(or_1_out), .in2(adder_1_out), .in6(subtractor_1_out), .out(Result), .sel(ALU_Op));  // open: in3, in4, in5, in7, in8, in9, in10, in11, in12, in13, in14, in15
  Comparator #(.width(32)) comparator_1 (.a(Result), .b({32{1'b0}}), .eq(Zero_Flag));  // open: gt, lt
endmodule

module Control (
  input  [5:0] Control_In,
  output Jump,
  output RegDst,
  output Branch,
  output MemRead,
  output MemToReg,
  output MemWrite,
  output ALUSrc,
  output [1:0] ALUOp,
  output RegWrite
);

  wire and_1_out, and_2_out, and_3_out;
  wire [1:0] bit_extender_1_out, bit_extender_2_out, shifter_1_out;

  and and_1 (and_1_out, ~Control_In[2], ~Control_In[5]);  // AND_Gate
  and and_2 (and_2_out, ~Control_In[2], ~Control_In[1]);  // AND_Gate
  and and_3 (and_3_out, Control_In[0], ~Control_In[3]);  // AND_Gate
  and and_4 (Jump, Control_In[1], ~Control_In[5]);  // AND_Gate
  and and_5 (RegDst, ~Control_In[1], ~Control_In[2]);  // AND_Gate
  and and_6 (MemRead, Control_In[0], ~Control_In[3]);  // AND_Gate
  assign bit_extender_1_out = {{1{1'b0}}, and_1_out};  // Bit_Extender bit_extender_1
  assign bit_extender_2_out = {{1{1'b0}}, Control_In[2]};  // Bit_Extender bit_extender_2
  or or_1 (RegWrite, and_2_out, and_3_out);
  Shifter #(.width(2)) shifter_1 (.in(bit_extender_1_out), .\dist (1'b1), .out(shifter_1_out));
  assign ALUOp = shifter_1_out | bit_extender_2_out;  // OR_Gate or_2, 2 bits wide

  assign ALUSrc = Control_In[1];
  assign Branch = Control_In[2];
  assign MemToReg = MemRead;
  assign MemWrite = Control_In[3];
endmodule

module ALUControl (
  input  [1:0] ALUOp,
  input  [5:0] _6bitfromISTR,
  output [3:0] ALU_Control_Out
);

  wire [1:1] not_1_out;

  not not_1 (not_1_out[1], _6bitfromISTR[2]);
  Multiplexer #(.select(2), .width(4), .enable("false")) multiplexer_1 (
    .in0(4'b0010), .in1(4'b0110), .in2({1'b0, _6bitfromISTR[1], not_1_out[1], _6bitfromISTR[0]}),
    .out(ALU_Control_Out), .sel(ALUOp));  // open: in3
endmodule
